# Fritzing sketch SCHEMATICS (saved by Fritzing 0.9.3b)
breadboards: 1

parts:
  Componente1 = Arduino Nano (Rev3.0)
  Matrix_keypad1 = KEYPAD 4x4
  LED1 = LED - 5mm [color="White (4500K)" package="5 mm [THT]"]
  LED2 = LED - 5mm [color="Green (555nm)" package="5 mm [THT]"]
  LED3 = LED - 5mm [color="Red (633nm)" package="5 mm [THT]"]
  LCD1 = LCD screen
  PIR1 = PIR sensor
  R1 = Rotary Potentiometer (Small) [maximum_resistance=100kΩ package=THT]
  R2 = Resistor [tolerance=±5% resistance=220 package="0603 [SMD]"]
  J1 = Piezo Speaker
  R3 = Resistor [tolerance=±5% resistance=220 package="0603 [SMD]"]
  LED4 = LED - 5mm [color="Yellow (595nm)" package="5 mm [THT]"]
  R4 = Resistor [tolerance=±5% resistance=220 package="0603 [SMD]"]
  R5 = Resistor [tolerance=±5% resistance=220 package="0603 [SMD]"]
  R6 = Resistor [tolerance=±5% resistance=220 package="0603 [SMD]"]

nets:
  GND: Componente1.GND, LED1.cathode, LED2.cathode, LED3.cathode, LCD1.VSS, LCD1.R/W, LCD1.LED-, PIR1.GND, R1.leg1, J1.pin1, LED4.cathode
  N1: Componente1.D2, R5.Pin_1
  N2: Componente1.D3, R4.Pin_1
  N3: Componente1.D4, R3.Pin_1
  N4: Componente1.D5, Matrix_keypad1.col1
  N5: Componente1.D6, Matrix_keypad1.col2
  N6: Componente1.D7, Matrix_keypad1.col3
  N7: Componente1.D8, Matrix_keypad1.col4
  N8: Componente1.D9, Matrix_keypad1.row1
  N9: Componente1.D10, Matrix_keypad1.row2
  N10: Componente1.D11/MOSI, Matrix_keypad1.row3
  N11: Componente1.D12/MISO, Matrix_keypad1.row4
  VDD: Componente1.5V, LCD1.VDD, PIR1.VDD, R1.leg2, R2.Pin_0
  N12: Componente1.A7, R6.Pin_1
  N13: Componente1.A6, J1.pin2
  N14: Componente1.A5, LCD1.DB7
  N15: Componente1.A4, LCD1.DB6
  N16: Componente1.A3, LCD1.DB5
  N17: Componente1.A2, LCD1.DB4
  N18: Componente1.A1, LCD1.E
  N19: Componente1.A0, LCD1.RS
  N20: Componente1.D13/SCK, PIR1.SIG
  N21: LED1.anode, R6.Pin_0
  N22: LED2.anode, R5.Pin_0
  N23: LED3.anode, R3.Pin_0
  N24: LCD1.V0, R1.wiper
  N25: LCD1.LED+, R2.Pin_1
  N26: LED4.anode, R4.Pin_0

custom parts:
  KEYPAD 4x4: Matrix keypad 16 buttons, 4 rows x 4 columns
